# Fritzing sketch fritzing_sketch (saved by Fritzing 0.9.3b)
circuit board: 8.46667cm x 5.64444cm

parts:
  U1 = ESP8266 NodeMCU LoLin module
  Part2 = RFID-RC522-v2
  U2 = LCD-16X2 [package=lcd-16x2]
  LCM1602_IIC2 = LCM1602 IIC [part_number="LCM1602 IIC" chip_label="LCM1602 IIC" package="DIP (Dual Inline) [THT]"]

nets:
  N1: U1.D0, Part2.RST
  N2: U1.D1, LCM1602_IIC2.SCL
  N3: U1.D2, LCM1602_IIC2.SDA
  3V3: U1.3V3, Part2.3.3V, LCM1602_IIC2.VCC
  GND: U1.GND, Part2.GND, LCM1602_IIC2.GND
  N4: U1.D5, Part2.SCK
  N5: U1.D6, Part2.MISO
  N6: U1.D7, Part2.MOSI
  N7: U1.D8, Part2.SDA
  VSS: U2.VSS, LCM1602_IIC2.VSS
  VDD: U2.VDD, LCM1602_IIC2.VDD
  N8: U2.VO, LCM1602_IIC2.V0
  N9: U2.RS, LCM1602_IIC2.RS
  N10: U2.R_W, LCM1602_IIC2.RW
  N11: U2.E, LCM1602_IIC2.E
  N12: U2.DB0, LCM1602_IIC2.D0
  N13: U2.DB1, LCM1602_IIC2.D1
  N14: U2.DB2, LCM1602_IIC2.D2
  N15: U2.DB3, LCM1602_IIC2.D3
  N16: U2.DB4, LCM1602_IIC2.D4
  N17: U2.DB5, LCM1602_IIC2.D5
  N18: U2.DB6, LCM1602_IIC2.D6
  N19: U2.DB7, LCM1602_IIC2.D7
  N20: U2.A, LCM1602_IIC2.A
  N21: U2.K, LCM1602_IIC2.K

custom parts:
  ESP8266 NodeMCU LoLin module: ESP8266 based NodeMCU
  RFID-RC522-v2: A simple China made RFID-RC522 Reader; do check the pin labels, as this is a MFRC522 based clone.
  LCM1602 IIC: I2C-Module to use a 1602 or 2004 LCD on with the wire.h libory Serial LCD Modul
